# Fritzing sketch midimultiplexer (saved by Fritzing 0.9.3b)
circuit board: 3.7cm x 5.4cm

parts:
  R1 = Resistor [tolerance=±5% resistance=10k package=THT]
  4067_Multiplexer = HCF 4067 [package="DIP24 [THT]"]
  Inputs_9-16 = double row female pin header, 16 pins [form="♀ (female)"]
  Inputs_1-8 = double row female pin header, 16 pins [form="♀ (female)"]
  3V3 = female pin header, 16 pins [form="♀ (female)"]
  10_-_13 = female pin header, 12 pins [form="♀ (female)"]

nets:
  N1: R1.Pin_0, 4067_Multiplexer.1_O/I, 3V3.pin5
  GND: R1.Pin_1, 4067_Multiplexer.12_VSS, 4067_Multiplexer.15_Inhibit, 3V3.pin4
  N2: 4067_Multiplexer.2_TG_7, Inputs_1-8.pin8
  N3: 4067_Multiplexer.3_TG6, Inputs_1-8.pin7
  N4: 4067_Multiplexer.4_TG5, Inputs_1-8.pin6
  N5: 4067_Multiplexer.5_TG4, Inputs_1-8.pin5
  N6: 4067_Multiplexer.6_TG3, Inputs_1-8.pin4
  N7: 4067_Multiplexer.7_TG2, Inputs_1-8.pin3
  N8: 4067_Multiplexer.8_TG1, Inputs_1-8.pin2
  N9: 4067_Multiplexer.9_TG0, Inputs_1-8.pin1
  N10: 4067_Multiplexer.10_A, 10_-_13.pin5
  N11: 4067_Multiplexer.11_B, 10_-_13.pin4
  N12: 4067_Multiplexer.13_D, 10_-_13.pin6
  N13: 4067_Multiplexer.14_C, 10_-_13.pin7
  N14: 4067_Multiplexer.16_TG15, Inputs_9-16.pin8
  N15: 4067_Multiplexer.17_TG14, Inputs_9-16.pin7
  N16: 4067_Multiplexer.18_TG13, Inputs_9-16.pin6
  N17: 4067_Multiplexer.19_TG12, Inputs_9-16.pin5
  N18: 4067_Multiplexer.20_TG11, Inputs_9-16.pin4
  N19: 4067_Multiplexer.21_TG10, Inputs_9-16.pin3
  N20: 4067_Multiplexer.22_TG9, Inputs_9-16.pin2
  N21: 4067_Multiplexer.23_TG8, Inputs_9-16.pin1
  3.3V: 4067_Multiplexer.24_Vdd, Inputs_9-16.pin9, Inputs_9-16.pin10, Inputs_9-16.pin11, Inputs_9-16.pin12, Inputs_9-16.pin13, Inputs_9-16.pin14, Inputs_9-16.pin15, Inputs_9-16.pin16, Inputs_1-8.pin9, Inputs_1-8.pin10, Inputs_1-8.pin11, Inputs_1-8.pin12, Inputs_1-8.pin13, Inputs_1-8.pin14, Inputs_1-8.pin15, Inputs_1-8.pin16, 3V3.pin2

notes:
  A0
  13
  12
  11
  10
  use tall
  headers so
  the feather
  can stack on
  Adafruit Feather
  GND
  3V3
  -
  +
  (on stacking headers)
